// Logisim project bit16.3.circ as structural Verilog: 4 circuits, main circuit main
module main (
);

  wire and_1_out, and_2_out, and_3_out, and_4_out, and_6_out, and_7_out, and_8_out, button_1_out,
       button_2_out, demultiplexer_1_out0, demultiplexer_1_out1, demultiplexer_1_out2, demultiplexer_1_out3,
       demultiplexer_1_out4, demultiplexer_1_out5, demultiplexer_1_out6, demultiplexer_1_out7,
       demultiplexer_2_out1, demultiplexer_2_out3, demultiplexer_2_out7, demultiplexer_2_out11,
       multiplexer_1_out, not_1_out, or_1_out, or_2_out, or_3_out, or_5_out, xnor_1_out, xnor_2_out,
       xor_1_out, xor_2_out;
  wire [2:0] rom_1_data_2;
  wire [3:0] multiplexer_10_out, multiplexer_14_out, nor_1_out, register_9_q;
  wire [5:0] multiplexer_3_out_2;
  wire [6:0] pla_1_out;
  wire [9:0] adder_1_out, multiplexer_2_out, multiplexer_3_out, register_7_q, register_8_q;
  wire [11:0] multiplexer_10_out_2;
  wire [12:0] rom_1_data;
  wire [15:0] adder_2_out, and_5_out, bit_extender_1_out, bit_extender_2_out, bit_extender_3_out,
       multiplexer_4_out, multiplexer_5_out, multiplexer_6_out, multiplexer_7_out, multiplexer_8_out,
       multiplexer_9_out, multiplexer_11_out, multiplexer_12_out, multiplexer_13_out, multiplexer_15_out,
       multiplier_1_out, myadder_1_out_3, negator_1_out, not_2_out, or_4_out, ram_1_dout, register_1_q,
       register_2_q, register_3_q, register_4_q, register_5_q, register_6_q, shifter_1_out, shifter_2_out,
       xor_3_out;

  or or_1 (or_1_out, register_9_q[0], xor_1_out);
  xor xor_1 (xor_1_out, register_9_q[1], register_9_q[2]);
  xnor xnor_1 (xnor_1_out, register_9_q[1], register_9_q[2]);
  not not_1 (not_1_out, register_9_q[0]);
  xor xor_2 (xor_2_out, register_9_q[1], register_9_q[2]);
  xnor xnor_2 (xnor_2_out, register_9_q[1], register_9_q[2]);
  and and_1 (and_1_out, ~register_9_q[0], xnor_2_out);  // AND_Gate
  or or_2 (or_2_out, and_2_out, and_3_out);
  and and_2 (and_2_out, ~rom_1_data[12], pla_1_out[0]);  // AND_Gate
  and and_3 (and_3_out, pla_1_out[5], ~or_5_out);  // AND_Gate
  Demultiplexer #(.select(3)) demultiplexer_1 (
    .out0(demultiplexer_1_out0), .out1(demultiplexer_1_out1), .out2(demultiplexer_1_out2),
    .out3(demultiplexer_1_out3), .out4(demultiplexer_1_out4), .out5(demultiplexer_1_out5),
    .out6(demultiplexer_1_out6), .out7(demultiplexer_1_out7), .in(or_2_out), .sel(rom_1_data[2:0]));
  Multiplexer #(.select(3)) multiplexer_1 (
    .in0(1'b1), .in1(register_9_q[0]), .in2(not_1_out), .in3(and_1_out), .in4(xor_2_out), .in5(xnor_1_out),
    .in6(or_1_out), .in7(1'b0), .out(multiplexer_1_out), .sel(rom_1_data[12:10]));
  and and_4 (and_4_out, multiplexer_1_out, pla_1_out[6]);
  or or_3 (or_3_out, and_4_out, demultiplexer_1_out7);
  Register #(.width(16)) register_1 (
    .D({multiplexer_3_out_2, multiplexer_3_out}), .en(demultiplexer_1_out0), .clk(button_2_out),
    .Q(register_1_q), .clr(button_1_out));
  Register #(.width(16)) register_2 (
    .D({multiplexer_3_out_2, multiplexer_3_out}), .en(demultiplexer_1_out1), .clk(button_2_out),
    .Q(register_2_q), .clr(button_1_out));
  Register #(.width(16)) register_3 (
    .D({multiplexer_3_out_2, multiplexer_3_out}), .en(demultiplexer_1_out2), .clk(button_2_out),
    .Q(register_3_q), .clr(button_1_out));
  Register #(.width(16)) register_4 (
    .D({multiplexer_3_out_2, multiplexer_3_out}), .en(demultiplexer_1_out3), .clk(button_2_out),
    .Q(register_4_q), .clr(button_1_out));
  Register #(.width(16)) register_5 (
    .D({multiplexer_3_out_2, multiplexer_3_out}), .en(demultiplexer_1_out4), .clk(button_2_out),
    .Q(register_5_q), .clr(button_1_out));
  Register #(.width(16)) register_6 (
    .D({multiplexer_3_out_2, multiplexer_3_out}), .en(demultiplexer_1_out5), .clk(button_2_out),
    .Q(register_6_q), .clr(button_1_out));
  Register #(.width(10)) register_7 (
    .D(multiplexer_3_out), .en(demultiplexer_1_out6), .clk(button_2_out), .Q(register_7_q), .clr(button_1_out));
  Register #(.width(10)) register_8 (
    .D(multiplexer_2_out), .en(1'b1), .clk(button_2_out), .Q(register_8_q), .clr(button_1_out));
  Multiplexer #(.width(10)) multiplexer_2 (
    .in0(adder_1_out), .in1(multiplexer_3_out), .out(multiplexer_2_out), .sel(or_3_out));
  Button button_1 (.out(button_1_out));
  Multiplexer #(.width(16)) multiplexer_3 (
    .in0(multiplexer_12_out), .in1({{6{1'b0}}, rom_1_data[9:0]}),
    .out({multiplexer_3_out_2, multiplexer_3_out}), .sel(pla_1_out[6]));
  Multiplexer #(.select(3), .width(16)) multiplexer_4 (
    .in0(register_1_q), .in1(register_2_q), .in2(register_3_q), .in3(register_4_q), .in4(register_5_q),
    .in5(register_6_q), .in6({{6{1'b0}}, register_7_q}), .in7({{6{1'b0}}, register_8_q}),
    .out(multiplexer_4_out), .sel(rom_1_data[2:0]));
  Multiplexer #(.select(3), .width(16)) multiplexer_5 (
    .in0(register_1_q), .in1(register_2_q), .in2(register_3_q), .in3(register_4_q), .in4(register_5_q),
    .in5(register_6_q), .in6({{6{1'b0}}, register_7_q}), .in7({{6{1'b0}}, register_8_q}),
    .out(multiplexer_5_out), .sel(rom_1_data[5:3]));
  Multiplexer #(.select(3), .width(16)) multiplexer_6 (
    .in0(register_1_q), .in1(register_2_q), .in2(register_3_q), .in3(register_4_q), .in4(register_5_q),
    .in5(register_6_q), .in6({{6{1'b0}}, register_7_q}), .in7({{6{1'b0}}, register_8_q}),
    .out(multiplexer_6_out), .sel(rom_1_data[8:6]));
  Adder #(.width(10)) adder_1 (.a(register_8_q), .b(10'h1), .out(adder_1_out));  // open: cin, cout
  Button button_2 (.out(button_2_out));
  ROM #(.addrWidth(10), .dataWidth(16)) rom_1 (.addr(register_8_q), .data({rom_1_data_2, rom_1_data}));
  Multiplexer #(.width(16)) multiplexer_7 (
    .in0(multiplexer_5_out), .in1(bit_extender_1_out), .out(multiplexer_7_out), .sel(pla_1_out[4]));
  assign bit_extender_1_out = {{10{rom_1_data[8]}}, rom_1_data[8:3]};  // Bit_Extender bit_extender_1
  Multiplexer #(.width(16)) multiplexer_8 (
    .in0(multiplexer_6_out), .in1(bit_extender_2_out), .out(multiplexer_8_out), .sel(pla_1_out[3]));
  assign bit_extender_2_out = {{12{rom_1_data[9]}}, rom_1_data[9:6]};  // Bit_Extender bit_extender_2
  Multiplexer #(.width(16)) multiplexer_9 (
    .in0(multiplexer_4_out), .in1(multiplexer_5_out), .out(multiplexer_9_out), .sel(pla_1_out[2]));
  Multiplexer #(.width(16)) multiplexer_10 (
    .in0(multiplexer_7_out), .in1(multiplexer_8_out), .out({multiplexer_10_out_2, multiplexer_10_out}),
    .sel(pla_1_out[2]));
  Negator #(.width(16)) negator_1 (.in({multiplexer_10_out_2, multiplexer_10_out}), .out(negator_1_out));
  Multiplier #(.width(16)) multiplier_1 (
    .a(multiplexer_9_out), .b({multiplexer_10_out_2, multiplexer_10_out}), .out(multiplier_1_out));  // open: cin, cout
  assign not_2_out = ~multiplexer_9_out;  // NOT_Gate not_2, 16 bits wide
  assign and_5_out = multiplexer_9_out & {multiplexer_10_out_2, multiplexer_10_out};  // AND_Gate and_5, 16 bits wide
  assign or_4_out = multiplexer_9_out | {multiplexer_10_out_2, multiplexer_10_out};  // OR_Gate or_4, 16 bits wide
  assign xor_3_out = multiplexer_9_out ^ {multiplexer_10_out_2, multiplexer_10_out};  // XOR_Gate xor_3, 16 bits wide
  Shifter #(.shift("lr"), .width(16)) shifter_1 (
    .in(multiplexer_9_out), .\dist (multiplexer_10_out), .out(shifter_1_out));
  Shifter #(.width(16)) shifter_2 (.in(multiplexer_9_out), .\dist (multiplexer_10_out), .out(shifter_2_out));
  PLA #(.in_width(3), .out_width(7), .\table ("000 0000000\n001 0100000\n010 0110000\n011 0100110\n100 0101110\n101 0100000\n110 0000001\n111 1000000")) pla_1 (
    .in(rom_1_data_2), .out(pla_1_out));
  MyAdder myadder_1 (
    .in_1(multiplexer_9_out), .in_2(multiplexer_11_out), .C(nor_1_out[3]), .v(nor_1_out[2]),
    .out_3(myadder_1_out_3));
  Multiplexer #(.width(16)) multiplexer_11 (
    .in0({multiplexer_10_out_2, multiplexer_10_out}), .in1(negator_1_out), .out(multiplexer_11_out),
    .sel(and_6_out));
  and and_6 (and_6_out, multiplexer_14_out[1], ~multiplexer_14_out[2], ~multiplexer_14_out[3]);  // AND_Gate
  Multiplexer #(.width(16)) multiplexer_12 (
    .in0(multiplexer_13_out), .in1(ram_1_dout), .out(multiplexer_12_out), .sel(and_7_out));
  Multiplexer #(.select(4), .width(16)) multiplexer_13 (
    .in0(myadder_1_out_3), .in1(myadder_1_out_3), .in2(myadder_1_out_3), .in3(myadder_1_out_3),
    .in4(multiplier_1_out), .in5(not_2_out), .in6(and_5_out), .in7(and_5_out), .in8(or_4_out),
    .in10(xor_3_out), .in11(xor_3_out), .in12(shifter_1_out), .in13(negator_1_out), .in14(shifter_2_out),
    .in15({multiplexer_10_out_2, multiplexer_10_out}), .out(multiplexer_13_out), .sel(multiplexer_14_out));  // open: in9
  or or_5 (or_5_out, demultiplexer_2_out1, demultiplexer_2_out3, demultiplexer_2_out7, demultiplexer_2_out11);
  Multiplexer #(.width(4)) multiplexer_14 (
    .in0(rom_1_data[12:9]), .in1({rom_1_data[12:10], 1'b0}), .out(multiplexer_14_out), .sel(pla_1_out[1]));
  and and_7 (and_7_out, pla_1_out[0], ~rom_1_data[12]);  // AND_Gate
  Demultiplexer #(.select(4)) demultiplexer_2 (
    .out1(demultiplexer_2_out1), .out3(demultiplexer_2_out3), .out7(demultiplexer_2_out7),
    .out11(demultiplexer_2_out11), .in(pla_1_out[5]), .sel(multiplexer_14_out));  // open: out0, out2, out4, out5, out6, out8, out9, out10, out12, out13, out14, out15
  nor nor_1 (nor_1_out[0], multiplexer_13_out[0], multiplexer_13_out[1], multiplexer_13_out[2], multiplexer_13_out[3], multiplexer_13_out[4], multiplexer_13_out[5], multiplexer_13_out[6], multiplexer_13_out[7], multiplexer_13_out[8], multiplexer_13_out[9], multiplexer_13_out[10], multiplexer_13_out[11], multiplexer_13_out[12], multiplexer_13_out[13], multiplexer_13_out[14], multiplexer_13_out[15]);
  Register #(.width(4)) register_9 (
    .D({nor_1_out[3:2], multiplexer_13_out[15], nor_1_out[0]}), .en(or_5_out), .clk(button_2_out),
    .Q(register_9_q));  // open: clr
  Multiplexer #(.width(16)) multiplexer_15 (
    .in0(multiplexer_6_out), .in1(bit_extender_3_out), .out(multiplexer_15_out), .sel(rom_1_data[11]));
  assign bit_extender_3_out = {{11{rom_1_data[10]}}, rom_1_data[10:6]};  // Bit_Extender bit_extender_3
  and and_8 (and_8_out, pla_1_out[0], rom_1_data[12]);
  Adder #(.width(16)) adder_2 (.a(multiplexer_5_out), .b(multiplexer_15_out), .out(adder_2_out));  // open: cin, cout
  RAM #(.addrWidth(16), .dataWidth(16), .enables("line")) ram_1 (
    .addr(adder_2_out), .we(and_8_out), .clk(button_2_out), .din(multiplexer_4_out), .dout(ram_1_dout));

  // Notes on the sheet:
  //   sp
  //   lr
  //   pc
  //   contents of rom_1 (hex, n*v repeats v):
  //   5e30 3e3e 401e e007 5e01 d808 e006 440d d82e 440d d829 440d d82a 440d d828 c829 4601 e814 5e09 e01c
  //   c829 c828 4408 3e3e 401e e007 3e02 2811 3e08 400d 400d cfea 400d cfe9 400d cfef
  //   7
  //   Rd
  //   1
  //   2
  //   Rs
  //   4
  //   6
  //   Rs2
  //   3
  //   CVNZ
endmodule

module Registers (
  input  Clk,
  input  [2:0] AS,
  input  [15:0] D,
  input  W,
  input  [2:0] BS,
  input  [2:0] RS,
  output [15:0] A,
  output [15:0] B,
  output [15:0] PC
);

  wire demultiplexer_1_out0, demultiplexer_1_out1, demultiplexer_1_out2, demultiplexer_1_out3,
       demultiplexer_1_out4, demultiplexer_1_out5, demultiplexer_1_out6, demultiplexer_1_out7;
  wire [15:0] register_1_q, register_2_q, register_3_q, register_4_q, register_5_q, register_6_q,
       register_7_q;

  Demultiplexer #(.select(3)) demultiplexer_1 (
    .out0(demultiplexer_1_out0), .out1(demultiplexer_1_out1), .out2(demultiplexer_1_out2),
    .out3(demultiplexer_1_out3), .out4(demultiplexer_1_out4), .out5(demultiplexer_1_out5),
    .out6(demultiplexer_1_out6), .out7(demultiplexer_1_out7), .in(W), .sel(RS));
  Register #(.width(16)) register_1 (.D(D), .en(demultiplexer_1_out0), .clk(Clk), .Q(register_1_q));  // open: clr
  Register #(.width(16)) register_2 (.D(D), .en(demultiplexer_1_out1), .clk(Clk), .Q(register_2_q));  // open: clr
  Register #(.width(16)) register_3 (.D(D), .en(demultiplexer_1_out2), .clk(Clk), .Q(register_3_q));  // open: clr
  Register #(.width(16)) register_4 (.D(D), .en(demultiplexer_1_out3), .clk(Clk), .Q(register_4_q));  // open: clr
  Register #(.width(16)) register_5 (.D(D), .en(demultiplexer_1_out4), .clk(Clk), .Q(register_5_q));  // open: clr
  Register #(.width(16)) register_6 (.D(D), .en(demultiplexer_1_out5), .clk(Clk), .Q(register_6_q));  // open: clr
  Register #(.width(16)) register_7 (.D(D), .en(demultiplexer_1_out6), .clk(Clk), .Q(register_7_q));  // open: clr
  Register #(.width(16)) register_8 (.D(D), .en(demultiplexer_1_out7), .clk(Clk), .Q(PC));  // open: clr
  Multiplexer #(.select(3), .width(16)) multiplexer_1 (
    .in0(register_1_q), .in1(register_2_q), .in2(register_3_q), .in3(register_4_q), .in4(register_5_q),
    .in5(register_6_q), .in6(register_7_q), .in7(PC), .out(A), .sel(AS));
  Multiplexer #(.select(3), .width(16)) multiplexer_2 (
    .in0(register_1_q), .in1(register_2_q), .in2(register_3_q), .in3(register_4_q), .in4(register_5_q),
    .in5(register_6_q), .in6(register_7_q), .in7(PC), .out(B), .sel(BS));
endmodule

module ALU (
  input  [3:0] OP,
  input  [15:0] A,
  input  [15:0] B,
  output [15:0] O,
  output [3:0] CVNZ
);

  wire and_2_out;
  wire [15:0] and_1_out, multiplexer_1_out, multiplier_1_out, myadder_1_out_3, negator_1_out, not_1_out,
       or_1_out, shifter_1_out, shifter_2_out, xor_1_out;

  Multiplexer #(.width(16)) multiplexer_1 (.in0(B), .in1(negator_1_out), .out(multiplexer_1_out), .sel(and_2_out));
  Negator #(.width(16)) negator_1 (.in(B), .out(negator_1_out));
  Multiplier #(.width(16)) multiplier_1 (.a(A), .b(B), .out(multiplier_1_out));  // open: cin, cout
  assign not_1_out = ~A;  // NOT_Gate not_1, 16 bits wide
  assign and_1_out = A & B;  // AND_Gate and_1, 16 bits wide
  assign or_1_out = A | B;  // OR_Gate or_1, 16 bits wide
  assign xor_1_out = A ^ B;  // XOR_Gate xor_1, 16 bits wide
  Shifter #(.shift("lr"), .width(16)) shifter_1 (.in(A), .\dist (B[3:0]), .out(shifter_1_out));
  Shifter #(.width(16)) shifter_2 (.in(A), .\dist (B[3:0]), .out(shifter_2_out));
  and and_2 (and_2_out, OP[1], ~OP[2], ~OP[3]);  // AND_Gate
  MyAdder myadder_1 (.in_1(A), .in_2(multiplexer_1_out), .C(CVNZ[3]), .v(CVNZ[2]), .out_3(myadder_1_out_3));
  Multiplexer #(.select(4), .width(16)) multiplexer_2 (
    .in0(myadder_1_out_3), .in1(myadder_1_out_3), .in2(myadder_1_out_3), .in3(myadder_1_out_3),
    .in4(multiplier_1_out), .in5(not_1_out), .in6(and_1_out), .in7(and_1_out), .in8(or_1_out),
    .in10(xor_1_out), .in11(xor_1_out), .in12(shifter_1_out), .in13(negator_1_out), .in14(shifter_2_out),
    .in15(B), .out({CVNZ[1], O[14:0]}), .sel(OP));  // open: in9
  nor nor_1 (CVNZ[0], O[0], O[1], O[2], O[3], O[4], O[5], O[6], O[7], O[8], O[9], O[10], O[11], O[12], O[13], O[14], CVNZ[1]);

  assign O[15] = CVNZ[1];
endmodule

module MyAdder (
  input  [15:0] in_1,
  input  [15:0] in_2,
  output [15:0] out_3,
  output C,
  output v
);

  wire adder_1_cout, adder_2_cout, adder_3_cout, adder_4_cout, adder_5_cout, adder_6_cout, adder_7_cout,
       adder_8_cout, adder_9_cout, adder_10_cout, adder_11_cout, adder_12_cout, adder_13_cout, adder_14_cout,
       adder_15_cout;

  Adder #(.width(1)) adder_1 (.a(in_1[0]), .b(in_2[0]), .out(out_3[0]), .cout(adder_1_cout));  // open: cin
  Adder #(.width(1)) adder_2 (.a(in_1[1]), .b(in_2[1]), .out(out_3[1]), .cin(adder_1_cout), .cout(adder_2_cout));
  Adder #(.width(1)) adder_3 (.a(in_1[2]), .b(in_2[2]), .out(out_3[2]), .cin(adder_2_cout), .cout(adder_3_cout));
  Adder #(.width(1)) adder_4 (.a(in_1[3]), .b(in_2[3]), .out(out_3[3]), .cin(adder_3_cout), .cout(adder_4_cout));
  Adder #(.width(1)) adder_5 (.a(in_1[4]), .b(in_2[4]), .out(out_3[4]), .cin(adder_4_cout), .cout(adder_5_cout));
  Adder #(.width(1)) adder_6 (.a(in_1[5]), .b(in_2[5]), .out(out_3[5]), .cin(adder_5_cout), .cout(adder_6_cout));
  Adder #(.width(1)) adder_7 (.a(in_1[6]), .b(in_2[6]), .out(out_3[6]), .cin(adder_6_cout), .cout(adder_7_cout));
  Adder #(.width(1)) adder_8 (.a(in_1[7]), .b(in_2[7]), .out(out_3[7]), .cin(adder_7_cout), .cout(adder_8_cout));
  Adder #(.width(1)) adder_9 (.a(in_1[8]), .b(in_2[8]), .out(out_3[8]), .cin(adder_8_cout), .cout(adder_9_cout));
  Adder #(.width(1)) adder_10 (.a(in_1[9]), .b(in_2[9]), .out(out_3[9]), .cin(adder_9_cout), .cout(adder_10_cout));
  Adder #(.width(1)) adder_11 (.a(in_1[10]), .b(in_2[10]), .out(out_3[10]), .cin(adder_10_cout), .cout(adder_11_cout));
  Adder #(.width(1)) adder_12 (.a(in_1[11]), .b(in_2[11]), .out(out_3[11]), .cin(adder_11_cout), .cout(adder_12_cout));
  Adder #(.width(1)) adder_13 (.a(in_1[12]), .b(in_2[12]), .out(out_3[12]), .cin(adder_12_cout), .cout(adder_13_cout));
  Adder #(.width(1)) adder_14 (.a(in_1[13]), .b(in_2[13]), .out(out_3[13]), .cin(adder_13_cout), .cout(adder_14_cout));
  Adder #(.width(1)) adder_15 (.a(in_1[14]), .b(in_2[14]), .out(out_3[14]), .cin(adder_14_cout), .cout(adder_15_cout));
  Adder #(.width(1)) adder_16 (.a(in_1[15]), .b(in_2[15]), .out(out_3[15]), .cin(adder_15_cout), .cout(C));
  xor xor_1 (v, adder_15_cout, C);
endmodule
