// Logisim project bit16.6.circ as structural Verilog: 3 circuits, main circuit main
module main (
);

  wire and_1_out, and_2_out, and_3_out, and_4_out, and_6_out, and_7_out, and_9_out, and_10_out, and_11_out,
       B_Const, button_2_out, Byte, C_Const, Clk, clock_1_out, Cond, demultiplexer_1_out0,
       demultiplexer_1_out1, demultiplexer_1_out2, demultiplexer_1_out3, demultiplexer_1_out4,
       demultiplexer_1_out5, demultiplexer_1_out6, demultiplexer_1_out7, demultiplexer_2_out1,
       demultiplexer_2_out3, demultiplexer_2_out7, demultiplexer_2_out11, j_k_ff_1_q, j_k_ff_1_qn, Jump,
       Latch, LatchF, LatchR, LdStr, not_1_out, Op, or_1_out, or_2_out, or_6_out, RAMW, reset, Word,
       xnor_1_out, xnor_2_out, xor_1_out, xor_2_out;
  wire [1:0] pla_1_out;
  wire [2:0] Const6, Rd;
  wire [3:0] comparator_1_eq, Const4, Flag, multiplexer_9_out, multiplexer_15_out;
  wire [6:0] keyboard_1_data;
  wire [7:7] Const8;
  wire [9:8] Offset10;
  wire [11:0] multiplexer_9_out_2;
  wire [15:0] A, A_q, adder_1_out, Addr, ALU, and_5_out, B, B_q, bit_extender_1_out, bit_extender_2_out,
       bit_extender_3_out, bit_extender_4_out, bit_extender_5_out, bit_extender_6_out, C, C_q, ConAddr, D_q,
       Data, FP_q, LR_q, multiplexer_2_out, multiplexer_3_out, multiplexer_7_out, multiplexer_8_out,
       multiplexer_10_out, multiplexer_12_out, multiplexer_14_out, multiplexer_18_out, multiplier_1_out,
       myadder_1_out_3, negator_1_out, not_2_out, or_4_out, PC, RAMout, shifter_1_out, shifter_2_out, SP_q,
       xor_3_out;
  wire [15:13] IR_q;

  Multiplexer #(.select(3)) multiplexer_1 (
    .in0(1'b0), .in1(Flag[0]), .in2(not_1_out), .in3(and_1_out), .in4(xor_1_out), .in5(xnor_2_out),
    .in6(or_1_out), .in7(1'b1), .out(Cond), .sel(Rd));
  Demultiplexer #(.select(3)) demultiplexer_1 (
    .out0(demultiplexer_1_out0), .out1(demultiplexer_1_out1), .out2(demultiplexer_1_out2),
    .out3(demultiplexer_1_out3), .out4(demultiplexer_1_out4), .out5(demultiplexer_1_out5),
    .out6(demultiplexer_1_out6), .out7(demultiplexer_1_out7), .in(LatchR), .sel(Rd));
  not not_1 (not_1_out, Flag[0]);
  and and_1 (and_1_out, ~Flag[0], xnor_1_out);  // AND_Gate
  xor xor_1 (xor_1_out, Flag[1], Flag[2]);
  xnor xnor_1 (xnor_1_out, Flag[1], Flag[2]);
  Register #(.trigger("falling"), .width(16)) u_A (
    .D(Data), .en(demultiplexer_1_out0), .clk(Clk), .Q(A_q), .clr(reset));
  Register #(.trigger("falling"), .width(16)) u_B (
    .D(Data), .en(demultiplexer_1_out1), .clk(Clk), .Q(B_q), .clr(reset));
  Register #(.trigger("falling"), .width(16)) u_C (
    .D(Data), .en(demultiplexer_1_out2), .clk(Clk), .Q(C_q), .clr(reset));
  Register #(.trigger("falling"), .width(16)) D (.D(Data), .en(demultiplexer_1_out3), .clk(Clk), .Q(D_q), .clr(reset));
  Register #(.trigger("falling"), .width(16)) FP (
    .D(Data), .en(demultiplexer_1_out4), .clk(Clk), .Q(FP_q), .clr(reset));
  Register #(.trigger("falling"), .width(16)) SP (
    .D(Data), .en(demultiplexer_1_out5), .clk(Clk), .Q(SP_q), .clr(reset));
  Register #(.trigger("falling"), .width(16)) LR (
    .D(Data), .en(demultiplexer_1_out6), .clk(Clk), .Q(LR_q), .clr(reset));
  Register #(.trigger("falling"), .width(16)) u_PC (.D(multiplexer_2_out), .en(1'b1), .clk(Clk), .Q(PC), .clr(reset));
  Multiplexer #(.width(16)) multiplexer_2 (
    .in0(adder_1_out), .in1(Data), .out(multiplexer_2_out), .sel(demultiplexer_1_out7));
  assign bit_extender_1_out = {{6{Offset10[9]}}, {Offset10, Const8[7], Const4, Const6}};  // Bit_Extender bit_extender_1
  xor xor_2 (xor_2_out, Flag[1], Flag[2]);
  xnor xnor_2 (xnor_2_out, Flag[1], Flag[2]);
  or or_1 (or_1_out, Flag[0], xor_2_out);
  and and_2 (and_2_out, Jump, Cond);
  Adder #(.width(16)) adder_1 (.a(PC), .b(multiplexer_3_out), .out(adder_1_out));  // open: cin, cout
  Multiplexer #(.width(16)) multiplexer_3 (
    .in0(16'h1), .in1(bit_extender_1_out), .out(multiplexer_3_out), .sel(and_2_out));
  Multiplexer #(.select(3), .width(16)) multiplexer_4 (
    .in0(A_q), .in1(B_q), .in2(C_q), .in3(D_q), .in4(FP_q), .in5(SP_q), .in6(LR_q), .in7(PC), .out(A),
    .sel(Rd));
  Multiplexer #(.select(3), .width(16)) multiplexer_5 (
    .in0(A_q), .in1(B_q), .in2(C_q), .in3(D_q), .in4(FP_q), .in5(SP_q), .in6(LR_q), .in7(PC), .out(B),
    .sel(Const6));
  Multiplexer #(.select(3), .width(16)) multiplexer_6 (
    .in0(A_q), .in1(B_q), .in2(C_q), .in3(D_q), .in4(FP_q), .in5(SP_q), .in6(LR_q), .in7(PC), .out(C),
    .sel(Const4[2:0]));
  RAM #(.addrWidth(16), .dataWidth(16), .enables("line"), .trigger("falling")) ram_1 (
    .addr(Addr), .we(RAMW), .clk(Clk), .din(A), .dout(RAMout));
  PLA #(.in_width(16), .\table ("01111111xxxxxxxx 01\n1000000000000000 10")) pla_1 (.in(Addr), .out(pla_1_out));
  TTY #(.trigger("falling")) tty_1 (.data(A[6:0]), .clk(Clk), .we(pla_1_out[0]), .clr(or_2_out));
  and and_3 (and_3_out, pla_1_out[0], ~Clk, A[7]);  // AND_Gate
  or or_2 (or_2_out, and_3_out, reset);
  Clock clock_1 (.out(clock_1_out));
  Button button_1 (.out(reset));
  and and_4 (and_4_out, Clk, pla_1_out[1]);
  Keyboard #(.trigger("falling")) keyboard_1 (
    .clk(and_4_out), .re(pla_1_out[1]), .clr(or_2_out), .data(keyboard_1_data));  // open: avail
  or or_3 (Clk, clock_1_out, button_2_out);
  Button button_2 (.out(button_2_out));
  Multiplexer #(.width(16)) multiplexer_7 (.in0(B), .in1(bit_extender_2_out), .out(multiplexer_7_out), .sel(B_Const));
  assign bit_extender_2_out = {{10{Const4[2]}}, {Const4[2:0], Const6}};  // Bit_Extender bit_extender_2
  assign bit_extender_3_out = {{12{Const4[3]}}, Const4};  // Bit_Extender bit_extender_3
  assign bit_extender_4_out = {{9{1'b0}}, keyboard_1_data};  // Bit_Extender bit_extender_4
  Multiplexer #(.width(16)) multiplexer_8 (.in0(A), .in1(B), .out(multiplexer_8_out), .sel(Op));
  Multiplexer #(.width(16)) multiplexer_9 (
    .in0(multiplexer_7_out), .in1(multiplexer_10_out), .out({multiplexer_9_out_2, multiplexer_9_out}),
    .sel(Op));
  Multiplexer #(.width(16)) multiplexer_10 (.in0(C), .in1(bit_extender_3_out), .out(multiplexer_10_out), .sel(C_Const));
  Multiplexer #(.width(16)) multiplexer_11 (.in1(bit_extender_4_out), .sel(pla_1_out[1]));  // open: in0, out
  Negator #(.width(16)) negator_1 (.in({multiplexer_9_out_2, multiplexer_9_out}), .out(negator_1_out));
  Multiplier #(.width(16)) multiplier_1 (
    .a(multiplexer_8_out), .b({multiplexer_9_out_2, multiplexer_9_out}), .out(multiplier_1_out));  // open: cin, cout
  assign not_2_out = ~multiplexer_8_out;  // NOT_Gate not_2, 16 bits wide
  assign and_5_out = multiplexer_8_out & {multiplexer_9_out_2, multiplexer_9_out};  // AND_Gate and_5, 16 bits wide
  assign or_4_out = multiplexer_8_out | {multiplexer_9_out_2, multiplexer_9_out};  // OR_Gate or_4, 16 bits wide
  assign xor_3_out = multiplexer_8_out ^ {multiplexer_9_out_2, multiplexer_9_out};  // XOR_Gate xor_3, 16 bits wide
  Multiplexer #(.width(16)) multiplexer_12 (
    .in0({multiplexer_9_out_2, multiplexer_9_out}), .in1(negator_1_out), .out(multiplexer_12_out),
    .sel(and_6_out));
  and and_6 (and_6_out, multiplexer_15_out[1], ~multiplexer_15_out[2], ~multiplexer_15_out[3]);  // AND_Gate
  Shifter #(.shift("lr"), .width(16)) shifter_1 (
    .in(multiplexer_8_out), .\dist (multiplexer_9_out), .out(shifter_1_out));
  Shifter #(.width(16)) shifter_2 (.in(multiplexer_8_out), .\dist (multiplexer_9_out), .out(shifter_2_out));
  or or_5 (LatchR, or_6_out, Byte, and_7_out);
  MyAdder myadder_1 (
    .in_1(multiplexer_8_out), .in_2(multiplexer_12_out), .C(comparator_1_eq[3]), .v(comparator_1_eq[2]),
    .out_3(myadder_1_out_3));
  Multiplexer #(.width(16)) multiplexer_13 (.in0(ALU), .in1(RAMout), .out(Data), .sel(or_6_out));
  or or_6 (or_6_out, and_10_out, and_11_out);
  and and_7 (and_7_out, Latch, ~LatchF);  // AND_Gate
  and and_8 (RAMW, LdStr, Offset10[9]);
  Multiplexer #(.select(4), .width(16)) multiplexer_14 (
    .in0(myadder_1_out_3), .in1(myadder_1_out_3), .in2(myadder_1_out_3), .in3(myadder_1_out_3),
    .in4(multiplier_1_out), .in5(not_2_out), .in6(and_5_out), .in7(and_5_out), .in8(or_4_out),
    .in10(xor_3_out), .in11(xor_3_out), .in12(shifter_1_out), .in13(negator_1_out), .in14(shifter_2_out),
    .in15({multiplexer_9_out_2, multiplexer_9_out}), .out(multiplexer_14_out), .sel(multiplexer_15_out));  // open: in9
  Multiplexer #(.width(4)) multiplexer_15 (
    .in0({Offset10, Const8[7], Const4[3]}), .in1({Offset10, Const8[7], 1'b0}), .out(multiplexer_15_out),
    .sel(Op));
  Multiplexer #(.width(16)) multiplexer_16 (.in0(PC), .in1(ConAddr), .out(Addr), .sel(and_9_out));
  and and_9 (and_9_out, Clk, j_k_ff_1_qn, LdStr);
  and and_10 (and_10_out, LdStr, ~Offset10[9]);  // AND_Gate
  and and_11 (and_11_out, Word, j_k_ff_1_q);
  Comparator #(.width(16)) comparator_1 (
    .a(multiplexer_14_out), .b({16{1'b0}}), .eq(comparator_1_eq[0]), .lt(comparator_1_eq[1]));  // open: gt
  or or_7 (LatchF, demultiplexer_2_out1, demultiplexer_2_out3, demultiplexer_2_out7, demultiplexer_2_out11);
  Demultiplexer #(.select(4)) demultiplexer_2 (
    .out1(demultiplexer_2_out1), .out3(demultiplexer_2_out3), .out7(demultiplexer_2_out7),
    .out11(demultiplexer_2_out11), .in(Latch), .sel(multiplexer_15_out));  // open: out0, out2, out4, out5, out6, out8, out9, out10, out12, out13, out14, out15
  J_K_Flip_Flop #(.trigger("falling")) j_k_ff_1 (
    .J(Word), .K(Word), .clk(Clk), .Q(j_k_ff_1_q), .Qn(j_k_ff_1_qn), .reset(reset));  // open: preset
  Multiplexer #(.width(16)) multiplexer_17 (.in0(multiplexer_14_out), .in1(bit_extender_5_out), .out(ALU), .sel(Byte));
  assign bit_extender_5_out = {{8{Const8[7]}}, {Const8[7], Const4, Const6}};  // Bit_Extender bit_extender_5
  Register #(.trigger("falling"), .width(4)) F (.D(comparator_1_eq), .en(LatchF), .clk(Clk), .Q(Flag), .clr(reset));
  Register #(.width(16)) IR (
    .D(RAMout), .en(j_k_ff_1_qn), .clk(Clk), .Q({IR_q, Offset10, Const8[7], Const4, Const6, Rd}), .clr(reset));
  PLA #(.in_width(3), .out_width(8), .\table ("000 00000001\n001 01000000\n010 00010000\n011 00011000\n100 00010010\n101 00010110\n110 00100000\n111 10000000")) pla_2 (
    .in(IR_q), .out({Word, Byte, LdStr, Latch, B_Const, C_Const, Op, Jump}));
  Multiplexer #(.width(16)) multiplexer_18 (
    .in0(C), .in1(bit_extender_6_out), .out(multiplexer_18_out), .sel(Offset10[8]));
  assign bit_extender_6_out = {{11{1'b0}}, {Const8[7], Const4}};  // Bit_Extender bit_extender_6
  Adder #(.width(16)) adder_2 (.a(B), .b(multiplexer_18_out), .out(ConAddr));  // open: cin, cout

  // Other names for the same wires on the sheet: Const8[6:0] = {Const4, Const6};
  //   Offset10[7:0] = {Const8[7], Const4, Const6}; Rs[2:0] = Const6; Const6[5:3] = Const4[2:0];
  //   Rs2[2:0] = Const4[2:0]; Op4[3:0] = {Offset10, Const8[7], Const4[3]}; Op3[2:0] = {Offset10, Const8[7]};
  //   S = Offset10[9]
endmodule

module MyAdder (
  input  [15:0] in_1,
  input  [15:0] in_2,
  output [15:0] out_3,
  output C,
  output v
);

  wire adder_1_cout, adder_2_cout, adder_3_cout, adder_4_cout, adder_5_cout, adder_6_cout, adder_7_cout,
       adder_8_cout, adder_9_cout, adder_10_cout, adder_11_cout, adder_12_cout, adder_13_cout, adder_14_cout,
       adder_15_cout;

  Adder #(.width(1)) adder_1 (.a(in_1[0]), .b(in_2[0]), .out(out_3[0]), .cout(adder_1_cout));  // open: cin
  Adder #(.width(1)) adder_2 (.a(in_1[1]), .b(in_2[1]), .out(out_3[1]), .cin(adder_1_cout), .cout(adder_2_cout));
  Adder #(.width(1)) adder_3 (.a(in_1[2]), .b(in_2[2]), .out(out_3[2]), .cin(adder_2_cout), .cout(adder_3_cout));
  Adder #(.width(1)) adder_4 (.a(in_1[3]), .b(in_2[3]), .out(out_3[3]), .cin(adder_3_cout), .cout(adder_4_cout));
  Adder #(.width(1)) adder_5 (.a(in_1[4]), .b(in_2[4]), .out(out_3[4]), .cin(adder_4_cout), .cout(adder_5_cout));
  Adder #(.width(1)) adder_6 (.a(in_1[5]), .b(in_2[5]), .out(out_3[5]), .cin(adder_5_cout), .cout(adder_6_cout));
  Adder #(.width(1)) adder_7 (.a(in_1[6]), .b(in_2[6]), .out(out_3[6]), .cin(adder_6_cout), .cout(adder_7_cout));
  Adder #(.width(1)) adder_8 (.a(in_1[7]), .b(in_2[7]), .out(out_3[7]), .cin(adder_7_cout), .cout(adder_8_cout));
  Adder #(.width(1)) adder_9 (.a(in_1[8]), .b(in_2[8]), .out(out_3[8]), .cin(adder_8_cout), .cout(adder_9_cout));
  Adder #(.width(1)) adder_10 (.a(in_1[9]), .b(in_2[9]), .out(out_3[9]), .cin(adder_9_cout), .cout(adder_10_cout));
  Adder #(.width(1)) adder_11 (.a(in_1[10]), .b(in_2[10]), .out(out_3[10]), .cin(adder_10_cout), .cout(adder_11_cout));
  Adder #(.width(1)) adder_12 (.a(in_1[11]), .b(in_2[11]), .out(out_3[11]), .cin(adder_11_cout), .cout(adder_12_cout));
  Adder #(.width(1)) adder_13 (.a(in_1[12]), .b(in_2[12]), .out(out_3[12]), .cin(adder_12_cout), .cout(adder_13_cout));
  Adder #(.width(1)) adder_14 (.a(in_1[13]), .b(in_2[13]), .out(out_3[13]), .cin(adder_13_cout), .cout(adder_14_cout));
  Adder #(.width(1)) adder_15 (.a(in_1[14]), .b(in_2[14]), .out(out_3[14]), .cin(adder_14_cout), .cout(adder_15_cout));
  Adder #(.width(1)) adder_16 (.a(in_1[15]), .b(in_2[15]), .out(out_3[15]), .cin(adder_15_cout), .cout(C));
  xor xor_1 (v, adder_15_cout, C);
endmodule

module scrtch (
);

  wire and_2_out, and_3_out, button_2_out, demultiplexer_1_out0, demultiplexer_1_out1, demultiplexer_1_out2,
       demultiplexer_1_out3, demultiplexer_1_out4, demultiplexer_1_out5, demultiplexer_1_out6,
       demultiplexer_1_out7, demultiplexer_2_out1, demultiplexer_2_out3, demultiplexer_2_out7,
       demultiplexer_2_out11, multiplexer_12_out, not_2_out, or_2_out, or_3_out, reset, undriven_2,
       undriven_3, undriven_6, undriven_7, undriven_8, undriven_9, undriven_12, xnor_1_out, xnor_2_out,
       xor_2_out, xor_3_out;
  wire [1:0] counter_2_q;
  wire [2:0] undriven_14;
  wire [3:0] multiplexer_7_out, multiplexer_9_out, nor_1_out, undriven_5;
  wire [3:1] undriven_10;
  wire [5:0] undriven_4;
  wire [7:0] rom_1_data;
  wire [11:0] multiplexer_7_out_2;
  wire [14:0] multiplexer_10_out;
  wire [15:0] adder_1_out, and_1_out, bit_extender_1_out, bit_extender_2_out, bit_extender_3_out,
       controlled_buffer_28_out, counter_1_q, multiplexer_1_out, multiplexer_2_out, multiplexer_3_out,
       multiplexer_4_out, multiplexer_5_out, multiplexer_6_out, multiplexer_8_out, multiplexer_11_out,
       multiplier_1_out, myadder_1_out_3, negator_1_out, not_1_out, or_1_out, register_1_q, register_2_q,
       register_3_q, register_4_q, register_5_q, register_6_q, register_7_q, register_9_q, shifter_1_out,
       shifter_2_out, undriven, undriven_11, undriven_13, xor_1_out;

  Controlled_Buffer #(.width(16)) controlled_buffer_1 ();  // open: in, out, en
  Controlled_Buffer #(.width(16)) controlled_buffer_2 ();  // open: in, out, en
  Controlled_Buffer #(.width(16)) controlled_buffer_3 ();  // open: in, out, en
  Controlled_Buffer #(.width(16)) controlled_buffer_4 ();  // open: in, out, en
  Controlled_Buffer #(.width(16)) controlled_buffer_5 ();  // open: in, out, en
  Controlled_Buffer #(.width(16)) controlled_buffer_6 ();  // open: in, out, en
  Controlled_Buffer #(.width(16)) controlled_buffer_7 ();  // open: in, out, en
  Controlled_Buffer #(.width(16)) controlled_buffer_8 ();  // open: in, out, en
  Controlled_Buffer #(.width(16)) controlled_buffer_9 ();  // open: in, out, en
  Controlled_Buffer #(.width(16)) controlled_buffer_10 ();  // open: in, out, en
  Controlled_Buffer #(.width(16)) controlled_buffer_11 ();  // open: in, out, en
  Controlled_Buffer #(.width(16)) controlled_buffer_12 ();  // open: in, out, en
  Controlled_Buffer #(.width(16)) controlled_buffer_13 ();  // open: in, out, en
  Controlled_Buffer #(.width(16)) controlled_buffer_14 ();  // open: in, out, en
  Controlled_Buffer #(.width(16)) controlled_buffer_15 ();  // open: in, out, en
  Controlled_Buffer #(.width(16)) controlled_buffer_16 ();  // open: in, out, en
  Controlled_Buffer #(.width(16)) controlled_buffer_17 ();  // open: in, out, en
  Controlled_Buffer #(.width(16)) controlled_buffer_18 ();  // open: in, out, en
  Controlled_Buffer #(.width(16)) controlled_buffer_19 ();  // open: in, out, en
  Controlled_Buffer #(.width(16)) controlled_buffer_20 ();  // open: in, out, en
  Controlled_Buffer #(.width(16)) controlled_buffer_21 ();  // open: in, out, en
  Controlled_Buffer #(.width(16)) controlled_buffer_22 ();  // open: in, out, en
  Demultiplexer #(.select(3)) demultiplexer_1 (
    .out0(demultiplexer_1_out0), .out1(demultiplexer_1_out1), .out2(demultiplexer_1_out2),
    .out3(demultiplexer_1_out3), .out4(demultiplexer_1_out4), .out5(demultiplexer_1_out5),
    .out6(demultiplexer_1_out6), .out7(demultiplexer_1_out7), .sel(register_9_q[2:0]));  // open: in
  Controlled_Buffer #(.width(16)) controlled_buffer_23 ();  // open: in, out, en
  Controlled_Buffer #(.width(16)) controlled_buffer_24 ();  // open: in, out, en
  Controlled_Buffer #(.width(16)) controlled_buffer_25 ();  // open: in, out, en
  Controlled_Buffer #(.width(16)) controlled_buffer_26 ();  // open: in, out, en
  Controlled_Buffer #(.width(16)) controlled_buffer_27 ();  // open: in, out, en
  Counter #(.max('hffff), .width(16)) counter_1 (
    .up(1'b1), .count(demultiplexer_1_out7), .clk(undriven_2), .Q(counter_1_q));  // open: clr, load, D, carry
  Register #(.trigger("falling"), .width(16)) register_1 (
    .D(undriven), .en(demultiplexer_1_out0), .clk(undriven_2), .Q(register_1_q), .clr(undriven_3));
  Register #(.trigger("falling"), .width(16)) register_2 (
    .D(undriven), .en(demultiplexer_1_out1), .clk(undriven_2), .Q(register_2_q), .clr(undriven_3));
  Register #(.trigger("falling"), .width(16)) register_3 (
    .D(undriven), .en(demultiplexer_1_out2), .clk(undriven_2), .Q(register_3_q), .clr(undriven_3));
  Register #(.trigger("falling"), .width(16)) register_4 (
    .D(undriven), .en(demultiplexer_1_out3), .clk(undriven_2), .Q(register_4_q), .clr(undriven_3));
  Register #(.trigger("falling"), .width(16)) register_5 (
    .D(undriven), .en(demultiplexer_1_out4), .clk(undriven_2), .Q(register_5_q), .clr(undriven_3));
  Register #(.trigger("falling"), .width(16)) register_6 (
    .D(undriven), .en(demultiplexer_1_out5), .clk(undriven_2), .Q(register_6_q), .clr(undriven_3));
  Register #(.trigger("falling"), .width(16)) register_7 (
    .D(undriven), .en(demultiplexer_1_out6), .clk(undriven_2), .Q(register_7_q), .clr(undriven_3));
  Button button_1 (.out(reset));
  Multiplexer #(.select(3), .width(16)) multiplexer_1 (
    .in0(register_1_q), .in1(register_2_q), .in2(register_3_q), .in3(register_4_q), .in4(register_5_q),
    .in5(register_6_q), .in6(register_7_q), .in7(counter_1_q), .out(multiplexer_1_out),
    .sel(register_9_q[2:0]));
  Multiplexer #(.select(3), .width(16)) multiplexer_2 (
    .in0(register_1_q), .in1(register_2_q), .in2(register_3_q), .in3(register_4_q), .in4(register_5_q),
    .in5(register_6_q), .in6(register_7_q), .in7(counter_1_q), .out(multiplexer_2_out),
    .sel(register_9_q[5:3]));
  Multiplexer #(.select(3), .width(16)) multiplexer_3 (
    .in0(register_1_q), .in1(register_2_q), .in2(register_3_q), .in3(register_4_q), .in4(register_5_q),
    .in5(register_6_q), .in6(register_7_q), .in7(counter_1_q), .out(multiplexer_3_out),
    .sel(register_9_q[8:6]));
  Button button_2 (.out(button_2_out));
  Controlled_Buffer #(.width(16)) controlled_buffer_28 (
    .in(multiplexer_1_out), .out(controlled_buffer_28_out));  // open: en
  Controlled_Buffer #(.width(16)) controlled_buffer_29 (.in(counter_1_q), .out(controlled_buffer_28_out));  // open: en
  Controlled_Buffer #(.width(16)) controlled_buffer_30 (
    .in({nor_1_out[1], multiplexer_10_out}), .out(controlled_buffer_28_out));  // open: en
  Register #(.width(16)) register_8 ();  // open: D, en, clk, Q, clr
  assign bit_extender_1_out = {{10{undriven_4[5]}}, undriven_4};  // Bit_Extender bit_extender_1
  assign bit_extender_2_out = {{12{undriven_5[3]}}, undriven_5};  // Bit_Extender bit_extender_2
  Multiplexer #(.width(16)) multiplexer_4 (
    .in0(multiplexer_2_out), .in1(bit_extender_1_out), .out(multiplexer_4_out), .sel(undriven_6));
  Multiplexer #(.width(16)) multiplexer_5 (
    .in0(multiplexer_3_out), .in1(bit_extender_2_out), .out(multiplexer_5_out), .sel(undriven_7));
  Multiplexer #(.width(16)) multiplexer_6 (
    .in0(multiplexer_1_out), .in1(multiplexer_2_out), .out(multiplexer_6_out), .sel(undriven_8));
  Multiplexer #(.width(16)) multiplexer_7 (
    .in0(multiplexer_4_out), .in1(multiplexer_5_out), .out({multiplexer_7_out_2, multiplexer_7_out}),
    .sel(undriven_8));
  Multiplexer #(.width(16)) multiplexer_8 (
    .in0({multiplexer_7_out_2, multiplexer_7_out}), .in1(negator_1_out), .out(multiplexer_8_out),
    .sel(and_2_out));
  Negator #(.width(16)) negator_1 (.in({multiplexer_7_out_2, multiplexer_7_out}), .out(negator_1_out));
  Multiplier #(.width(16)) multiplier_1 (
    .a(multiplexer_6_out), .b({multiplexer_7_out_2, multiplexer_7_out}), .out(multiplier_1_out));  // open: cin, cout
  assign not_1_out = ~multiplexer_6_out;  // NOT_Gate not_1, 16 bits wide
  assign and_1_out = multiplexer_6_out & {multiplexer_7_out_2, multiplexer_7_out};  // AND_Gate and_1, 16 bits wide
  assign or_1_out = multiplexer_6_out | {multiplexer_7_out_2, multiplexer_7_out};  // OR_Gate or_1, 16 bits wide
  assign xor_1_out = multiplexer_6_out ^ {multiplexer_7_out_2, multiplexer_7_out};  // XOR_Gate xor_1, 16 bits wide
  Shifter #(.shift("lr"), .width(16)) shifter_1 (
    .in(multiplexer_6_out), .\dist (multiplexer_7_out), .out(shifter_1_out));
  Shifter #(.width(16)) shifter_2 (.in(multiplexer_6_out), .\dist (multiplexer_7_out), .out(shifter_2_out));
  Counter #(.max('h3), .width(2)) counter_2 (.D(2'b00), .Q(counter_2_q));  // open: clr, load, up, count, clk, carry
  MyAdder myadder_1 (
    .in_1(multiplexer_6_out), .in_2(multiplexer_8_out), .C(nor_1_out[3]), .v(nor_1_out[2]),
    .out_3(myadder_1_out_3));
  and and_2 (and_2_out, multiplexer_9_out[1], ~multiplexer_9_out[2], ~multiplexer_9_out[3]);  // AND_Gate
  Register #(.width(16)) register_9 (.Q(register_9_q));  // open: D, en, clk, clr
  Multiplexer #(.width(4)) multiplexer_9 (
    .in1({undriven_10, 1'b0}), .out(multiplexer_9_out), .sel(undriven_9));  // open: in0
  ROM #(.addrWidth(5)) rom_1 (.addr({register_9_q[15:13], counter_2_q}), .data(rom_1_data));
  Multiplexer #(.select(4), .width(16)) multiplexer_10 (
    .in0(myadder_1_out_3), .in1(myadder_1_out_3), .in2(myadder_1_out_3), .in3(myadder_1_out_3),
    .in4(multiplier_1_out), .in5(not_1_out), .in6(and_1_out), .in7(and_1_out), .in8(or_1_out),
    .in10(xor_1_out), .in11(xor_1_out), .in12(shifter_1_out), .in13(negator_1_out), .in14(shifter_2_out),
    .in15({multiplexer_7_out_2, multiplexer_7_out}), .out({nor_1_out[1], multiplexer_10_out}),
    .sel(multiplexer_9_out));  // open: in9
  or or_2 (or_2_out, demultiplexer_2_out1, demultiplexer_2_out3, demultiplexer_2_out7, demultiplexer_2_out11);
  Demultiplexer #(.select(4)) demultiplexer_2 (
    .out1(demultiplexer_2_out1), .out3(demultiplexer_2_out3), .out7(demultiplexer_2_out7),
    .out11(demultiplexer_2_out11), .sel(multiplexer_9_out));  // open: out0, out2, out4, out5, out6, out8, out9, out10, out12, out13, out14, out15, in
  nor nor_1 (nor_1_out[0], multiplexer_10_out[0], multiplexer_10_out[1], multiplexer_10_out[2], multiplexer_10_out[3], multiplexer_10_out[4], multiplexer_10_out[5], multiplexer_10_out[6], multiplexer_10_out[7], multiplexer_10_out[8], multiplexer_10_out[9], multiplexer_10_out[10], multiplexer_10_out[11], multiplexer_10_out[12], multiplexer_10_out[13], multiplexer_10_out[14], nor_1_out[1]);
  Register #(.trigger("falling"), .width(4)) register_10 (.D(nor_1_out), .en(or_2_out));  // open: clk, Q, clr
  PLA #(.in_width(8), .out_width(8), .\table ("00000000 00000000\n00000001 00100000\n00000010 00110000\n00000011 00100110\n00000100 00101110\n00000101 00100000\n00000110 01000000\n00000111 00000001")) pla_1 (.in(rom_1_data));  // open: out
  PLA #(.in_width(3), .out_width(7), .\table ("000 0000000\n001 0100000\n010 0110000\n011 0100110\n100 0101110\n101 0100000\n110 1000000\n111 0000001")) pla_2 ();  // open: in, out
  RAM #(.addrWidth(16), .dataWidth(16), .enables("line"), .trigger("falling")) ram_1 ();  // open: addr, we, clk, din, dout
  Bit_Extender #(.in_width(5)) bit_extender_3 (.out(bit_extender_3_out));  // open: in
  Adder #(.width(16)) adder_1 (.a(undriven_13), .b(multiplexer_11_out), .out(adder_1_out));  // open: cin, cout
  Multiplexer #(.width(16)) multiplexer_11 (
    .in0(undriven_11), .in1(bit_extender_3_out), .out(multiplexer_11_out), .sel(undriven_12));
  or or_3 (or_3_out, undriven_14[0], xor_2_out);
  xor xor_2 (xor_2_out, undriven_14[1], undriven_14[2]);
  xnor xnor_1 (xnor_1_out, undriven_14[1], undriven_14[2]);
  not not_2 (not_2_out, undriven_14[0]);
  xor xor_3 (xor_3_out, undriven_14[1], undriven_14[2]);
  xnor xnor_2 (xnor_2_out, undriven_14[1], undriven_14[2]);
  and and_3 (and_3_out, ~undriven_14[0], xnor_2_out);  // AND_Gate
  Multiplexer #(.select(3)) multiplexer_12 (
    .in0(1'b1), .in1(undriven_14[0]), .in2(not_2_out), .in3(and_3_out), .in4(xor_3_out), .in5(xnor_1_out),
    .in6(or_3_out), .in7(1'b0), .out(multiplexer_12_out));  // open: sel
  // AND_Gate and_4 has open pins: in0=multiplexer_12_out, out=open

  // Notes on the sheet:
  //   sp
  //   lr
  //   7
  //   Rd
  //   1
  //   2
  //   Rs
  //   4
  //   CVNZ
  //   Rs2
  //   6
  //   3
endmodule
