// Logisim project bit16.9.circ as structural Verilog: 3 circuits, main circuit main
module main (
);

  wire ALU, and_1_out, and_2_out, and_3_out, and_4_out, and_5_out, and_6_out, and_7_out, and_8_out,
       and_10_out, and_11_out, and_13_out, and_14_out, and_15_out, and_16_out, and_17_out, button_1_out,
       button_2_out, button_3_out, Byte, Clk, clock_1_out, demultiplexer_1_out0, demultiplexer_1_out1,
       demultiplexer_1_out2, demultiplexer_1_out3, demultiplexer_1_out4, demultiplexer_1_out5,
       demultiplexer_1_out6, demultiplexer_1_out7, demultiplexer_2_out0, demultiplexer_2_out1, j_k_ff_1_q,
       j_k_ff_1_qn, Jump, LatchF, LatchR, Load, not_1_out, not_2_out, not_3_out, not_4_out, not_5_out,
       Offset, or_1_out, or_2_out, or_3_out, or_7_out, or_9_out, Reg3, Reset, RW, Stack, True, Word,
       xnor_1_out, xnor_2_out, xor_1_out, xor_2_out;
  wire [0:0] Op4;
  wire [2:0] IR_q, Rd, Rs;
  wire [3:0] comparator_1_eq, Cond, CVNZ, multiplexer_11_out, multiplexer_17_out, Op2;
  wire [6:0] keyboard_1_data;
  wire [7:6] IR_q_2;
  wire [11:0] multiplexer_11_out_2;
  wire [15:0] A_q, adder_1_out, adder_2_out, adder_3_out, Addr, and_9_out, Arg, B_q, Base,
       bit_extender_1_out, C_q, Const5, Const8, D_q, Data, Din, divider_1_out, divider_1_rem, Dout, FPBase,
       LR_q, multiplexer_2_out, multiplexer_3_out, multiplexer_4_out, multiplexer_8_out, multiplexer_9_out,
       multiplexer_10_out, multiplexer_12_out, multiplexer_13_out, multiplexer_15_out, multiplexer_16_out,
       multiplier_1_out, myadder_1_add, negator_1_out, not_6_out, Offset9, or_6_out, PC, Primary, ram_1_dout,
       shifter_1_out, shifter_2_out, SP, SP_q, xor_3_out;

  Multiplexer #(.select(4)) multiplexer_1 (
    .in0(1'b0), .in1(CVNZ[0]), .in2(not_1_out), .in3(CVNZ[1]), .in4(not_2_out), .in5(CVNZ[2]),
    .in6(not_3_out), .in7(CVNZ[3]), .in8(not_4_out), .in9(and_1_out), .in10(or_2_out), .in11(xor_1_out),
    .in12(xnor_1_out), .in13(or_3_out), .in14(and_3_out), .in15(1'b1), .out(True), .sel(Cond));
  Demultiplexer #(.select(3)) demultiplexer_1 (
    .out0(demultiplexer_1_out0), .out1(demultiplexer_1_out1), .out2(demultiplexer_1_out2),
    .out3(demultiplexer_1_out3), .out4(demultiplexer_1_out4), .out5(demultiplexer_1_out5),
    .out6(demultiplexer_1_out6), .out7(demultiplexer_1_out7), .in(LatchR), .sel(Rd));
  not not_1 (not_1_out, CVNZ[0]);
  not not_2 (not_2_out, CVNZ[1]);
  not not_3 (not_3_out, CVNZ[2]);
  not not_4 (not_4_out, CVNZ[3]);
  Multiplexer #(.width(16)) multiplexer_2 (
    .in0(adder_2_out), .in1(Data), .out(multiplexer_2_out), .sel(demultiplexer_1_out6));
  or or_1 (or_1_out, demultiplexer_1_out6, Stack);
  Multiplexer #(.width(16)) multiplexer_3 (
    .in0(adder_1_out), .in1(Data), .out(multiplexer_3_out), .sel(demultiplexer_1_out7));
  and and_1 (and_1_out, ~CVNZ[0], CVNZ[3]);  // AND_Gate
  or or_2 (or_2_out, CVNZ[0], ~CVNZ[3]);  // OR_Gate
  Register #(.trigger("falling"), .width(16)) A (.D(Data), .en(demultiplexer_1_out0), .clk(Clk), .Q(A_q), .clr(Reset));
  Register #(.trigger("falling"), .width(16)) B (.D(Data), .en(demultiplexer_1_out1), .clk(Clk), .Q(B_q), .clr(Reset));
  Register #(.trigger("falling"), .width(16)) C (.D(Data), .en(demultiplexer_1_out2), .clk(Clk), .Q(C_q), .clr(Reset));
  Register #(.trigger("falling"), .width(16)) D (.D(Data), .en(demultiplexer_1_out3), .clk(Clk), .Q(D_q), .clr(Reset));
  Register #(.trigger("falling"), .width(16)) LR (
    .D(Data), .en(demultiplexer_1_out4), .clk(Clk), .Q(LR_q), .clr(Reset));
  Register #(.trigger("falling"), .width(16)) FP (
    .D(Data), .en(demultiplexer_1_out5), .clk(Clk), .Q(FPBase), .clr(Reset));
  Register #(.trigger("falling"), .width(16)) u_SP (
    .D(multiplexer_2_out), .en(or_1_out), .clk(Clk), .Q(SP_q), .clr(Reset));
  Register #(.trigger("falling"), .width(16)) u_PC (.D(multiplexer_3_out), .en(1'b1), .clk(Clk), .Q(PC), .clr(Reset));
  xor xor_1 (xor_1_out, CVNZ[1], CVNZ[2]);
  xnor xnor_1 (xnor_1_out, CVNZ[1], CVNZ[2]);
  Multiplexer #(.width(16)) multiplexer_4 (.in0(16'h1), .in1(Offset9), .out(multiplexer_4_out), .sel(and_2_out));
  and and_2 (and_2_out, Jump, True);
  xor xor_2 (xor_2_out, CVNZ[1], CVNZ[2]);
  or or_3 (or_3_out, CVNZ[0], xor_2_out);
  and and_3 (and_3_out, ~CVNZ[0], xnor_2_out);  // AND_Gate
  Multiplexer #(.select(3), .width(16)) multiplexer_5 (
    .in0(A_q), .in1(B_q), .in2(C_q), .in3(D_q), .in4(LR_q), .in5(FPBase), .in6(SP_q), .in7(PC),
    .out(Primary), .sel(Rd));
  Multiplexer #(.select(3), .width(16)) multiplexer_6 (
    .in0(A_q), .in1(B_q), .in2(C_q), .in3(D_q), .in4(LR_q), .in5(FPBase), .in6(SP_q), .in7(PC), .out(Arg),
    .sel(Rs));
  Multiplexer #(.select(3), .width(16)) multiplexer_7 (
    .in0(A_q), .in1(B_q), .in2(C_q), .in3(D_q), .in4(LR_q), .in5(FPBase), .in6(SP_q), .in7(PC), .out(Base),
    .sel({Cond[1:0], Op4[0]}));
  and and_4 (and_4_out, Stack, Cond[2]);
  and and_5 (and_5_out, Stack, ~Cond[2]);  // AND_Gate
  Subtractor #(.width(16)) subtractor_1 (.a(SP_q), .b({16{1'b0}}), .out(SP), .bin(and_4_out));  // open: bout
  Adder #(.width(16)) adder_1 (.a(PC), .b(multiplexer_4_out), .out(adder_1_out));  // open: cin, cout
  xnor xnor_2 (xnor_2_out, CVNZ[1], CVNZ[2]);
  Adder #(.width(16)) adder_2 (.a(SP), .b({16{1'b0}}), .out(adder_2_out), .cin(and_5_out));  // open: cout
  not not_5 (not_5_out, Addr[15]);
  Demultiplexer #(.select(2)) demultiplexer_2 (
    .out0(demultiplexer_2_out0), .out1(demultiplexer_2_out1), .in(Addr[15]), .sel(Addr[1:0]));  // open: out2, out3
  Button button_1 (.out(button_1_out));
  RAM #(.addrWidth(15), .clearpin("true"), .dataWidth(16), .enables("line"), .trigger("falling")) ram_1 (
    .addr(Addr[14:0]), .we(and_6_out), .clk(Clk), .din(Dout), .dout(ram_1_dout), .clr(button_1_out));
  and and_6 (and_6_out, not_5_out, RW);
  TTY #(.trigger("falling")) tty_1 (.data(Dout[6:0]), .clk(Clk), .we(demultiplexer_2_out0), .clr(Reset));
  or or_4 (Reset, button_1_out, button_2_out);
  Button button_2 (.out(button_2_out));
  and and_7 (and_7_out, Clk, demultiplexer_2_out1);
  Keyboard #(.trigger("falling")) keyboard_1 (
    .clk(and_7_out), .re(demultiplexer_2_out1), .clr(Reset), .data(keyboard_1_data));  // open: avail
  or or_5 (Clk, clock_1_out, button_3_out);
  Clock clock_1 (.out(clock_1_out));
  Button button_3 (.out(button_3_out));
  assign bit_extender_1_out = {{9{1'b0}}, keyboard_1_data};  // Bit_Extender bit_extender_1
  and and_8 (and_8_out, ~RW, not_5_out);  // AND_Gate
  assign Din = and_8_out ? ram_1_dout : 16'bz;  // Controlled_Buffer controlled_buffer_1
  assign Din = demultiplexer_2_out1 ? bit_extender_1_out : 16'bz;  // Controlled_Buffer controlled_buffer_2
  Multiplexer #(.width(16)) multiplexer_8 (.in0(Arg), .in1(Const5), .out(multiplexer_8_out), .sel(Cond[3]));
  Multiplexer #(.width(16)) multiplexer_9 (.in0(Base), .in1(FPBase), .out(multiplexer_9_out), .sel(Cond[3]));
  Multiplexer #(.width(16)) multiplexer_10 (.in0(Const5), .in1(Const8), .out(multiplexer_10_out), .sel(Cond[3]));
  assign not_6_out = ~{multiplexer_11_out_2, multiplexer_11_out};  // NOT_Gate not_6, 16 bits wide
  Multiplexer #(.width(16)) multiplexer_11 (
    .in0(multiplexer_8_out), .in1(Const8), .out({multiplexer_11_out_2, multiplexer_11_out}), .sel(Byte));
  assign and_9_out = Primary & {multiplexer_11_out_2, multiplexer_11_out};  // AND_Gate and_9, 16 bits wide
  assign or_6_out = Primary | {multiplexer_11_out_2, multiplexer_11_out};  // OR_Gate or_6, 16 bits wide
  Adder #(.width(16)) adder_3 (.a(multiplexer_9_out), .b(multiplexer_12_out), .out(adder_3_out));  // open: cin, cout
  Multiplexer #(.width(16)) multiplexer_12 (.in0(multiplexer_10_out), .in1(Arg), .out(multiplexer_12_out), .sel(Reg3));
  assign Data = or_7_out ? Din : 16'bz;  // Controlled_Buffer controlled_buffer_3
  or or_7 (or_7_out, ~Clk, or_9_out);  // OR_Gate
  or or_8 (LatchR, or_9_out, Offset, and_15_out);
  Multiplexer #(.width(16)) multiplexer_13 (
    .in0({multiplexer_11_out_2, multiplexer_11_out}), .in1(not_6_out), .out(multiplexer_13_out),
    .sel(and_16_out));
  Negator #(.width(16)) negator_1 (.in({multiplexer_11_out_2, multiplexer_11_out}), .out(negator_1_out));
  Multiplier #(.width(16)) multiplier_1 (
    .a(Primary), .b({multiplexer_11_out_2, multiplexer_11_out}), .out(multiplier_1_out));  // open: cin, cout
  Divider #(.width(16)) divider_1 (
    .a(Primary), .b({multiplexer_11_out_2, multiplexer_11_out}), .out(divider_1_out), .rem(divider_1_rem));  // open: upper
  assign xor_3_out = Primary ^ {multiplexer_11_out_2, multiplexer_11_out};  // XOR_Gate xor_3, 16 bits wide
  Shifter #(.shift("lr"), .width(16)) shifter_1 (.in(Primary), .\dist (multiplexer_11_out), .out(shifter_1_out));
  Shifter #(.width(16)) shifter_2 (.in(Primary), .\dist (multiplexer_11_out), .out(shifter_2_out));
  and and_10 (and_10_out, Offset, Clk);
  assign Data = and_10_out ? adder_3_out : 16'bz;  // Controlled_Buffer controlled_buffer_4
  Multiplexer #(.width(16)) multiplexer_14 (.in0(PC), .in1(multiplexer_15_out), .out(Addr), .sel(and_11_out));
  Multiplexer #(.width(16)) multiplexer_15 (.in0(adder_3_out), .in1(SP), .out(multiplexer_15_out), .sel(Stack));
  and and_11 (and_11_out, Clk, j_k_ff_1_qn, Load);
  and and_12 (RW, Clk, Load, Cond[2]);
  assign Dout = RW ? Primary : 16'bz;  // Controlled_Buffer controlled_buffer_5
  and and_13 (and_13_out, Load, ~Cond[2]);  // AND_Gate
  or or_9 (or_9_out, and_13_out, and_14_out);
  and and_14 (and_14_out, Word, j_k_ff_1_q);
  and and_15 (and_15_out, ALU, ~LatchF);  // AND_Gate
  MyAdder myadder_1 (
    .a(Primary), .b(multiplexer_13_out), .cin(and_16_out), .cout(comparator_1_eq[3]), .add(myadder_1_add),
    .v(comparator_1_eq[2]));
  and and_16 (and_16_out, multiplexer_17_out[1], ~multiplexer_17_out[2], ~multiplexer_17_out[3]);  // AND_Gate
  J_K_Flip_Flop #(.trigger("falling")) j_k_ff_1 (
    .J(Word), .K(Word), .clk(Clk), .Q(j_k_ff_1_q), .Qn(j_k_ff_1_qn), .reset(Reset));  // open: preset
  Register #(.width(16)) IR (
    .D(Data), .en(j_k_ff_1_qn), .clk(Clk), .Q({IR_q, Cond, Op4[0], IR_q_2, Rs, Rd}), .clr(Reset));
  assign Data = and_17_out ? multiplexer_16_out : 16'bz;  // Controlled_Buffer controlled_buffer_6
  Multiplexer #(.select(4), .width(16)) multiplexer_16 (
    .in0({multiplexer_11_out_2, multiplexer_11_out}), .in1(myadder_1_add), .in2(myadder_1_add),
    .in3(myadder_1_add), .in4(not_6_out), .in5(negator_1_out), .in8(multiplier_1_out), .in9(divider_1_out),
    .in10(divider_1_rem), .in11(and_9_out), .in12(or_6_out), .in13(xor_3_out), .in14(shifter_1_out),
    .in15(shifter_2_out), .out(multiplexer_16_out), .sel(multiplexer_17_out));  // open: in6, in7
  and and_17 (and_17_out, Clk, ALU);
  Multiplexer #(.width(4)) multiplexer_17 (.in0({Cond[2:0], Op4[0]}), .in1(Op2), .out(multiplexer_17_out), .sel(Byte));
  PLA #(.in_width(3), .out_width(8), .\table ("000 00000001\n001 00000010\n010 00000110\n011 00001000\n100 00010000\n101 00110000\n110 01010000\n111 10000000")) pla_1 (
    .in(IR_q), .out({Word, Stack, Reg3, Load, Offset, Byte, ALU, Jump}));
  Comparator #(.width(16)) comparator_1 (.a(Data), .b({16{1'b0}}), .eq(comparator_1_eq[0]));  // open: gt, lt
  and and_18 (LatchF, ALU, multiplexer_17_out[0], multiplexer_17_out[1], ~multiplexer_17_out[2], ~multiplexer_17_out[3]);  // AND_Gate
  assign Const5 = {{11{IR_q_2[7]}}, {IR_q_2, Rs}};  // Bit_Extender bit_extender_2
  assign Const8 = {{8{1'b0}}, {Cond[1:0], Op4[0], IR_q_2, Rs}};  // Bit_Extender bit_extender_3
  assign Op2 = {{2{1'b0}}, Cond[3:2]};  // Bit_Extender bit_extender_4
  assign Offset9 = {{7{Op4[0]}}, {Op4[0], IR_q_2, Rs, Rd}};  // Bit_Extender bit_extender_5
  Register #(.trigger("falling"), .width(4)) Flag (
    .D({comparator_1_eq[3:2], Data[15], comparator_1_eq[0]}), .en(LatchF), .clk(Clk), .Q(CVNZ), .clr(Reset));

  // Other names for the same wires on the sheet: Op1 = Cond[2]; Op4[3:1] = Cond[2:0]; Mode = Cond[3];
  //   Rb[2:0] = {Cond[1:0], Op4[0]}
endmodule

module MyAdder (
  input  [15:0] a,
  input  cin,
  input  [15:0] b,
  output [15:0] add,
  output cout,
  output v
);

  wire adder_1_cout;

  Adder #(.width(15)) adder_1 (.a(a[14:0]), .b(b[14:0]), .out(add[14:0]), .cin(cin), .cout(adder_1_cout));
  Adder #(.width(1)) adder_2 (.a(a[15]), .b(b[15]), .out(add[15]), .cin(adder_1_cout), .cout(cout));
  xor xor_1 (v, adder_1_cout, cout);
endmodule

module scrtch (
  input  Lod,
  input  Op,
  output LatchR,
  output RamRead
);

  wire and_1_out, and_2_out, and_3_out, and_4_out, and_5_out, and_6_out, and_7_out, and_8_out, and_9_out,
       and_10_out, and_11_out, and_12_out, and_13_out, and_15_out, and_16_out, button_2_out,
       demultiplexer_1_out0, demultiplexer_1_out1, demultiplexer_1_out2, demultiplexer_1_out3,
       demultiplexer_1_out4, demultiplexer_1_out5, demultiplexer_1_out6, demultiplexer_1_out7,
       demultiplexer_2_out1, demultiplexer_2_out3, demultiplexer_2_out7, demultiplexer_2_out11,
       multiplexer_12_out, not_2_out, or_3_out, or_8_out, or_10_out, or_11_out, reset, undriven, undriven_2,
       undriven_4, undriven_5, undriven_8, undriven_9, undriven_10, undriven_11, undriven_14, xnor_1_out,
       xnor_2_out, xor_2_out, xor_3_out;
  wire [1:0] counter_2_q;
  wire [2:0] undriven_16;
  wire [3:0] multiplexer_7_out, multiplexer_9_out, nor_1_out, undriven_7;
  wire [3:1] undriven_12;
  wire [5:0] undriven_6;
  wire [7:0] rom_1_data;
  wire [11:0] multiplexer_7_out_2;
  wire [14:0] multiplexer_10_out;
  wire [15:0] adder_1_out, and_14_out, bit_extender_1_out, bit_extender_2_out, bit_extender_3_out,
       controlled_buffer_28_out, counter_1_q, multiplexer_1_out, multiplexer_2_out, multiplexer_3_out,
       multiplexer_4_out, multiplexer_5_out, multiplexer_6_out, multiplexer_8_out, multiplexer_11_out,
       multiplier_1_out, myadder_1_add, negator_1_out, not_1_out, or_9_out, register_1_q, register_2_q,
       register_3_q, register_4_q, register_5_q, register_6_q, register_7_q, register_9_q, shifter_1_out,
       shifter_2_out, undriven_3, undriven_13, undriven_15, xor_1_out;

  Controlled_Buffer #(.width(16)) controlled_buffer_1 ();  // open: in, out, en
  Controlled_Buffer #(.width(16)) controlled_buffer_2 ();  // open: in, out, en
  Controlled_Buffer #(.width(16)) controlled_buffer_3 ();  // open: in, out, en
  Controlled_Buffer #(.width(16)) controlled_buffer_4 ();  // open: in, out, en
  Controlled_Buffer #(.width(16)) controlled_buffer_5 ();  // open: in, out, en
  Controlled_Buffer #(.width(16)) controlled_buffer_6 ();  // open: in, out, en
  Controlled_Buffer #(.width(16)) controlled_buffer_7 ();  // open: in, out, en
  Controlled_Buffer #(.width(16)) controlled_buffer_8 ();  // open: in, out, en
  Controlled_Buffer #(.width(16)) controlled_buffer_9 ();  // open: in, out, en
  Controlled_Buffer #(.width(16)) controlled_buffer_10 ();  // open: in, out, en
  Controlled_Buffer #(.width(16)) controlled_buffer_11 ();  // open: in, out, en
  Controlled_Buffer #(.width(16)) controlled_buffer_12 ();  // open: in, out, en
  Controlled_Buffer #(.width(16)) controlled_buffer_13 ();  // open: in, out, en
  Controlled_Buffer #(.width(16)) controlled_buffer_14 ();  // open: in, out, en
  Controlled_Buffer #(.width(16)) controlled_buffer_15 ();  // open: in, out, en
  Controlled_Buffer #(.width(16)) controlled_buffer_16 ();  // open: in, out, en
  Controlled_Buffer #(.width(16)) controlled_buffer_17 ();  // open: in, out, en
  Controlled_Buffer #(.width(16)) controlled_buffer_18 ();  // open: in, out, en
  Controlled_Buffer #(.width(16)) controlled_buffer_19 ();  // open: in, out, en
  Controlled_Buffer #(.width(16)) controlled_buffer_20 ();  // open: in, out, en
  Controlled_Buffer #(.width(16)) controlled_buffer_21 ();  // open: in, out, en
  Controlled_Buffer #(.width(16)) controlled_buffer_22 ();  // open: in, out, en
  Demultiplexer #(.select(3)) demultiplexer_1 (
    .out0(demultiplexer_1_out0), .out1(demultiplexer_1_out1), .out2(demultiplexer_1_out2),
    .out3(demultiplexer_1_out3), .out4(demultiplexer_1_out4), .out5(demultiplexer_1_out5),
    .out6(demultiplexer_1_out6), .out7(demultiplexer_1_out7), .sel(register_9_q[2:0]));  // open: in
  Controlled_Buffer #(.width(16)) controlled_buffer_23 ();  // open: in, out, en
  Controlled_Buffer #(.width(16)) controlled_buffer_24 ();  // open: in, out, en
  Controlled_Buffer #(.width(16)) controlled_buffer_25 ();  // open: in, out, en
  Controlled_Buffer #(.width(16)) controlled_buffer_26 ();  // open: in, out, en
  Controlled_Buffer #(.width(16)) controlled_buffer_27 ();  // open: in, out, en
  and and_1 (and_1_out, ~undriven_2, Lod, ~Op);  // AND_Gate
  // OR_Gate or_1 has open pins: in0=and_1_out, in1=and_2_out, out=open
  and and_2 (and_2_out, undriven_2, ~Lod, ~Op);  // AND_Gate
  and and_3 (and_3_out, ~undriven_2, Lod, ~Op);  // AND_Gate
  // OR_Gate or_2 has open pins: in0=and_3_out, in1=and_4_out, out=open
  and and_4 (and_4_out, undriven_2, ~Lod, ~undriven, ~Op);  // AND_Gate
  and and_5 (and_5_out, Lod, ~Op);  // AND_Gate
  and and_6 (and_6_out, undriven_2, ~Op);  // AND_Gate
  and and_7 (and_7_out, Lod, ~Op);  // AND_Gate
  and and_8 (and_8_out, undriven_2, ~undriven, ~Op);  // AND_Gate
  and and_9 (and_9_out, undriven_2, ~Op);  // AND_Gate
  and and_10 (and_10_out, Lod, ~Op);  // AND_Gate
  or or_3 (or_3_out, undriven_2, Lod);
  and and_11 (and_11_out, or_3_out, ~Op);  // AND_Gate
  and and_12 (and_12_out, undriven_2, ~Op, ~undriven);  // AND_Gate
  Counter #(.max('hffff), .width(16)) counter_1 (
    .up(1'b1), .count(demultiplexer_1_out7), .clk(undriven_4), .Q(counter_1_q));  // open: clr, load, D, carry
  // OR_Gate or_4 has open pins: in0=and_5_out, in1=and_6_out, out=open
  // OR_Gate or_5 has open pins: in0=and_7_out, in1=and_8_out, out=open
  and and_13 (and_13_out, ~undriven, and_9_out);  // AND_Gate
  or or_6 (LatchR, and_13_out, and_10_out);
  or or_7 (RamRead, and_9_out, and_10_out);
  or or_8 (or_8_out, and_11_out, and_12_out);
  Register #(.trigger("falling"), .width(16)) register_1 (
    .D(undriven_3), .en(demultiplexer_1_out0), .clk(undriven_4), .Q(register_1_q), .clr(undriven_5));
  Register #(.trigger("falling"), .width(16)) register_2 (
    .D(undriven_3), .en(demultiplexer_1_out1), .clk(undriven_4), .Q(register_2_q), .clr(undriven_5));
  Register #(.trigger("falling"), .width(16)) register_3 (
    .D(undriven_3), .en(demultiplexer_1_out2), .clk(undriven_4), .Q(register_3_q), .clr(undriven_5));
  Register #(.trigger("falling"), .width(16)) register_4 (
    .D(undriven_3), .en(demultiplexer_1_out3), .clk(undriven_4), .Q(register_4_q), .clr(undriven_5));
  Register #(.trigger("falling"), .width(16)) register_5 (
    .D(undriven_3), .en(demultiplexer_1_out4), .clk(undriven_4), .Q(register_5_q), .clr(undriven_5));
  Register #(.trigger("falling"), .width(16)) register_6 (
    .D(undriven_3), .en(demultiplexer_1_out5), .clk(undriven_4), .Q(register_6_q), .clr(undriven_5));
  Register #(.trigger("falling"), .width(16)) register_7 (
    .D(undriven_3), .en(demultiplexer_1_out6), .clk(undriven_4), .Q(register_7_q), .clr(undriven_5));
  Button button_1 (.out(reset));
  Multiplexer #(.select(3), .width(16)) multiplexer_1 (
    .in0(register_1_q), .in1(register_2_q), .in2(register_3_q), .in3(register_4_q), .in4(register_5_q),
    .in5(register_6_q), .in6(register_7_q), .in7(counter_1_q), .out(multiplexer_1_out),
    .sel(register_9_q[2:0]));
  Multiplexer #(.select(3), .width(16)) multiplexer_2 (
    .in0(register_1_q), .in1(register_2_q), .in2(register_3_q), .in3(register_4_q), .in4(register_5_q),
    .in5(register_6_q), .in6(register_7_q), .in7(counter_1_q), .out(multiplexer_2_out),
    .sel(register_9_q[5:3]));
  Multiplexer #(.select(3), .width(16)) multiplexer_3 (
    .in0(register_1_q), .in1(register_2_q), .in2(register_3_q), .in3(register_4_q), .in4(register_5_q),
    .in5(register_6_q), .in6(register_7_q), .in7(counter_1_q), .out(multiplexer_3_out),
    .sel(register_9_q[8:6]));
  Button button_2 (.out(button_2_out));
  Controlled_Buffer #(.width(16)) controlled_buffer_28 (
    .in(multiplexer_1_out), .out(controlled_buffer_28_out));  // open: en
  Controlled_Buffer #(.width(16)) controlled_buffer_29 (.in(counter_1_q), .out(controlled_buffer_28_out));  // open: en
  Controlled_Buffer #(.width(16)) controlled_buffer_30 (
    .in({nor_1_out[1], multiplexer_10_out}), .out(controlled_buffer_28_out));  // open: en
  Register #(.width(16)) register_8 ();  // open: D, en, clk, Q, clr
  assign bit_extender_1_out = {{10{undriven_6[5]}}, undriven_6};  // Bit_Extender bit_extender_1
  assign bit_extender_2_out = {{12{undriven_7[3]}}, undriven_7};  // Bit_Extender bit_extender_2
  Multiplexer #(.width(16)) multiplexer_4 (
    .in0(multiplexer_2_out), .in1(bit_extender_1_out), .out(multiplexer_4_out), .sel(undriven_8));
  Multiplexer #(.width(16)) multiplexer_5 (
    .in0(multiplexer_3_out), .in1(bit_extender_2_out), .out(multiplexer_5_out), .sel(undriven_9));
  Multiplexer #(.width(16)) multiplexer_6 (
    .in0(multiplexer_1_out), .in1(multiplexer_2_out), .out(multiplexer_6_out), .sel(undriven_10));
  Multiplexer #(.width(16)) multiplexer_7 (
    .in0(multiplexer_4_out), .in1(multiplexer_5_out), .out({multiplexer_7_out_2, multiplexer_7_out}),
    .sel(undriven_10));
  Multiplexer #(.width(16)) multiplexer_8 (
    .in0({multiplexer_7_out_2, multiplexer_7_out}), .in1(negator_1_out), .out(multiplexer_8_out),
    .sel(and_15_out));
  Negator #(.width(16)) negator_1 (.in({multiplexer_7_out_2, multiplexer_7_out}), .out(negator_1_out));
  Multiplier #(.width(16)) multiplier_1 (
    .a(multiplexer_6_out), .b({multiplexer_7_out_2, multiplexer_7_out}), .out(multiplier_1_out));  // open: cin, cout
  assign not_1_out = ~multiplexer_6_out;  // NOT_Gate not_1, 16 bits wide
  assign and_14_out = multiplexer_6_out & {multiplexer_7_out_2, multiplexer_7_out};  // AND_Gate and_14, 16 bits wide
  assign or_9_out = multiplexer_6_out | {multiplexer_7_out_2, multiplexer_7_out};  // OR_Gate or_9, 16 bits wide
  assign xor_1_out = multiplexer_6_out ^ {multiplexer_7_out_2, multiplexer_7_out};  // XOR_Gate xor_1, 16 bits wide
  Shifter #(.shift("lr"), .width(16)) shifter_1 (
    .in(multiplexer_6_out), .\dist (multiplexer_7_out), .out(shifter_1_out));
  Shifter #(.width(16)) shifter_2 (.in(multiplexer_6_out), .\dist (multiplexer_7_out), .out(shifter_2_out));
  Counter #(.max('h3), .width(2)) counter_2 (.D(2'b00), .Q(counter_2_q));  // open: clr, load, up, count, clk, carry
  MyAdder myadder_1 (
    .a(multiplexer_6_out), .b(multiplexer_8_out), .cout(nor_1_out[3]), .add(myadder_1_add), .v(nor_1_out[2]));  // open: cin
  and and_15 (and_15_out, multiplexer_9_out[1], ~multiplexer_9_out[2], ~multiplexer_9_out[3]);  // AND_Gate
  Register #(.width(16)) register_9 (.Q(register_9_q));  // open: D, en, clk, clr
  Multiplexer #(.width(4)) multiplexer_9 (
    .in1({undriven_12, 1'b0}), .out(multiplexer_9_out), .sel(undriven_11));  // open: in0
  ROM #(.addrWidth(5)) rom_1 (.addr({register_9_q[15:13], counter_2_q}), .data(rom_1_data));
  Multiplexer #(.select(4), .width(16)) multiplexer_10 (
    .in0(myadder_1_add), .in1(myadder_1_add), .in2(myadder_1_add), .in3(myadder_1_add),
    .in4(multiplier_1_out), .in5(not_1_out), .in6(and_14_out), .in7(and_14_out), .in8(or_9_out),
    .in10(xor_1_out), .in11(xor_1_out), .in12(shifter_1_out), .in13(negator_1_out), .in14(shifter_2_out),
    .in15({multiplexer_7_out_2, multiplexer_7_out}), .out({nor_1_out[1], multiplexer_10_out}),
    .sel(multiplexer_9_out));  // open: in9
  or or_10 (or_10_out, demultiplexer_2_out1, demultiplexer_2_out3, demultiplexer_2_out7, demultiplexer_2_out11);
  Demultiplexer #(.select(4)) demultiplexer_2 (
    .out1(demultiplexer_2_out1), .out3(demultiplexer_2_out3), .out7(demultiplexer_2_out7),
    .out11(demultiplexer_2_out11), .sel(multiplexer_9_out));  // open: out0, out2, out4, out5, out6, out8, out9, out10, out12, out13, out14, out15, in
  nor nor_1 (nor_1_out[0], multiplexer_10_out[0], multiplexer_10_out[1], multiplexer_10_out[2], multiplexer_10_out[3], multiplexer_10_out[4], multiplexer_10_out[5], multiplexer_10_out[6], multiplexer_10_out[7], multiplexer_10_out[8], multiplexer_10_out[9], multiplexer_10_out[10], multiplexer_10_out[11], multiplexer_10_out[12], multiplexer_10_out[13], multiplexer_10_out[14], nor_1_out[1]);
  Register #(.trigger("falling"), .width(4)) register_10 (.D(nor_1_out), .en(or_10_out));  // open: clk, Q, clr
  PLA #(.in_width(8), .out_width(8), .\table ("00000000 00000000\n00000001 00100000\n00000010 00110000\n00000011 00100110\n00000100 00101110\n00000101 00100000\n00000110 01000000\n00000111 00000001")) pla_1 (.in(rom_1_data));  // open: out
  PLA #(.in_width(3), .out_width(7), .\table ("000 0000000\n001 0100000\n010 0110000\n011 0100110\n100 0101110\n101 0100000\n110 1000000\n111 0000001")) pla_2 ();  // open: in, out
  RAM #(.addrWidth(16), .dataWidth(16), .enables("line"), .trigger("falling")) ram_1 ();  // open: addr, we, clk, din, dout
  Bit_Extender #(.in_width(5)) bit_extender_3 (.out(bit_extender_3_out));  // open: in
  Adder #(.width(16)) adder_1 (.a(undriven_15), .b(multiplexer_11_out), .out(adder_1_out));  // open: cin, cout
  Multiplexer #(.width(16)) multiplexer_11 (
    .in0(undriven_13), .in1(bit_extender_3_out), .out(multiplexer_11_out), .sel(undriven_14));
  or or_11 (or_11_out, undriven_16[0], xor_2_out);
  xor xor_2 (xor_2_out, undriven_16[1], undriven_16[2]);
  xnor xnor_1 (xnor_1_out, undriven_16[1], undriven_16[2]);
  not not_2 (not_2_out, undriven_16[0]);
  xor xor_3 (xor_3_out, undriven_16[1], undriven_16[2]);
  xnor xnor_2 (xnor_2_out, undriven_16[1], undriven_16[2]);
  and and_16 (and_16_out, ~undriven_16[0], xnor_2_out);  // AND_Gate
  Multiplexer #(.select(3)) multiplexer_12 (
    .in0(1'b1), .in1(undriven_16[0]), .in2(not_2_out), .in3(and_16_out), .in4(xor_3_out), .in5(xnor_1_out),
    .in6(or_11_out), .in7(1'b0), .out(multiplexer_12_out));  // open: sel
  // AND_Gate and_17 has open pins: in0=multiplexer_12_out, out=open

  // Notes on the sheet:
  //   sp
  //   lr
  //   7
  //   Rd
  //   1
  //   2
  //   Rs
  //   4
  //   CVNZ
  //   Rs2
  //   6
  //   3
endmodule
